// Digital circuit divider.dig as structural Verilog
module divider (
  input  clk_i,
  input  reset_i,
  input  [3:0] dividend_i,
  input  [3:0] divisor_i,
  input  start_i,
  output busy_o,
  output finish_o,
  output [4:0] quotient_o
);

  wire and_1_out, div___eq__0_eq, not_1_out, not_2_out, not_3_out, or_1_out, sub__gt__eq__div_eq,
       sub__gt__eq__div_gt;
  wire [1:0] ns_logic_1_q0next;
  wire [3:0] multiplexer_1_out, sub_div_s, subtrahend_q;
  wire [4:0] multiplexer_2_out, multiplexer_4_out, quotient__plus__1_s, quotient_q;

  Comparator #(.Bits(4)) div___eq__0 (.a(divisor_i), .b(4'b0000), .eq(div___eq__0_eq));  // open: gt, lt
  not not_1 (not_1_out, div___eq__0_eq);
  ns_logic ns_logic_1 (
    .Q0(finish_o), .Q_1(busy_o), .start_i(start_i), .divisor_not_0(not_1_out),
    .subtrahend_gt_divisor(or_1_out), .Q0next(ns_logic_1_q0next[1]), .Q1next(ns_logic_1_q0next[0]));
  not not_2 (not_2_out, not_1_out);
  and and_1 (and_1_out, not_2_out, start_i);
  Sub #(.Bits(4)) sub_div (.a(subtrahend_q), .b(divisor_i), .c_i(1'b0), .s(sub_div_s));  // open: c_o
  D_FF_AS #(.Bits(2)) state (
    .Set(1'b0), .D(ns_logic_1_q0next), .C(clk_i), .Clr(reset_i), .Q({finish_o, busy_o}));  // open: nQ
  not not_3 (not_3_out, and_1_out);
  Multiplexer #(.Selector_Bits(2), .Bits(4)) multiplexer_1 (
    .sel({finish_o, busy_o}), .in_0(dividend_i), .in_1(sub_div_s), .in_2(subtrahend_q), .in_3(4'b0000),
    .out(multiplexer_1_out));
  D_FF_AS #(.Bits(4)) subtrahend (
    .Set(1'b0), .D(multiplexer_1_out), .C(clk_i), .Clr(reset_i), .Q(subtrahend_q));  // open: nQ
  Multiplexer #(.Bits(5)) multiplexer_2 (.sel(not_3_out), .in_0({5{1'b1}}), .in_1(quotient_q), .out(multiplexer_2_out));
  Multiplexer #(.Selector_Bits(2), .Bits(5)) multiplexer_3 (
    .sel({finish_o, busy_o}), .in_0({5{1'b0}}), .in_1(multiplexer_4_out), .in_2(multiplexer_2_out),
    .in_3({5{1'b0}}), .out(quotient_o));
  Comparator #(.Bits(4)) sub__gt__eq__div (
    .a(subtrahend_q), .b(divisor_i), .gt(sub__gt__eq__div_gt), .eq(sub__gt__eq__div_eq));  // open: lt
  or or_1 (or_1_out, sub__gt__eq__div_gt, sub__gt__eq__div_eq);
  D_FF_AS #(.Bits(5)) quotient (.Set(1'b0), .D(quotient_o), .C(clk_i), .Clr(reset_i), .Q(quotient_q));  // open: nQ
  Add #(.Bits(5)) quotient__plus__1 (.a(quotient_q), .b(5'b00001), .c_i(1'b0), .s(quotient__plus__1_s));  // open: c_o
  Multiplexer #(.Bits(5)) multiplexer_4 (
    .sel(or_1_out), .in_0(quotient_q), .in_1(quotient__plus__1_s), .out(multiplexer_4_out));

  // Notes on the sheet:
  //   clk_i: Hz: 2
  //   Q00 = Init
  //   Q01 = Busy
  //   Q10 = Finish
  //   Q11 = ---- (x)
endmodule
