// Digital circuit ns_logic.dig as structural Verilog
module ns_logic (
  input  Q0,
  input  Q_1,
  input  start_i,
  input  divisor_not_0,
  input  subtrahend_gt_divisor,
  output Q0next,
  output Q1next
);

  wire and_1_out, and_2_out, and_3_out, and_4_out, not_1_out, not_2_out, not_3_out, not_4_out;

  not not_1 (not_1_out, Q0);
  not not_2 (not_2_out, Q_1);
  not not_3 (not_3_out, divisor_not_0);
  not not_4 (not_4_out, subtrahend_gt_divisor);
  and and_1 (and_1_out, not_1_out, not_2_out, not_3_out, start_i);
  and and_2 (and_2_out, Q_1, not_4_out);
  and and_3 (and_3_out, not_1_out, not_2_out, divisor_not_0, start_i);
  and and_4 (and_4_out, Q_1, subtrahend_gt_divisor);
  or or_1 (Q0next, and_1_out, and_2_out);
  or or_2 (Q1next, and_3_out, and_4_out);
endmodule
